# Fritzing sketch rx (saved by Fritzing 0.9.3b)
circuit board: 8.46667cm x 5.64444cm
stripboards: 1

parts:
  HC-1 = HC-12 Module
  Antenna1 = HC-12 Antenna
  Teensy_3_1 = Teensy 3.0 [part_number="Freescale ARM MK20DX128"]
  KY-1 = Keyes Relay [package=THT]
  KY-2 = Keyes Relay [package=THT]

nets:
  N1: HC-1.SET, Teensy_3_1.2
  N2: HC-1.TXD, Teensy_3_1.1
  N3: HC-1.RXD, HC-1.GND, Teensy_3_1.AGND, Teensy_3_1.0, KY-1.ground, KY-2.ground
  VCC: HC-1.VCC, Teensy_3_1.Vin, KY-1.power, KY-2.power
  N4: HC-1.ANT, Antenna1.ANT
  N5: Teensy_3_1.23, KY-1.signal
  N6: Teensy_3_1.22, KY-2.signal

custom parts:
  HC-12 Module: HC-12 433Mhz Module
  HC-12 Antenna: Antenna for HC-12 433Mhz Module
  Keyes Relay: The Keyes 5V relay module is suitable for SCM development, home appliance control. It uses a 5V~12V TIL control signal which can control DC / AC signal.
