# Fritzing sketch tx (saved by Fritzing 0.9.3b)
circuit board: 8.46667cm x 5.64444cm
stripboards: 1

parts:
  HC-1 = HC-12 Module
  Antenna1 = HC-12 Antenna
  S1 = Taiway 100-SP-X-T1 SPDT Miniature Toggle Switch [part_number=100-SP-X-T1-0-0-B1-M1 package=THT]
  S2 = Taiway 100-SP-X-T1 SPDT Miniature Toggle Switch [part_number=100-SP-X-T1-0-0-B1-M1 package=THT]
  Teensy_3_1 = Teensy 3.0 [part_number="Freescale ARM MK20DX128"]

nets:
  N1: HC-1.SET, Teensy_3_1.2
  N2: HC-1.TXD, Teensy_3_1.1
  N3: HC-1.RXD, HC-1.GND, Teensy_3_1.AGND, Teensy_3_1.0
  VCC: HC-1.VCC, Teensy_3_1.Vin
  N4: HC-1.ANT, Antenna1.ANT
  N5: S1.COM, S2.COM, Teensy_3_1.3.3V#2
  N6: S1.L1, Teensy_3_1.15
  N7: S1.L2, Teensy_3_1.14
  N8: S2.L1, Teensy_3_1.19
  N9: S2.L2, Teensy_3_1.20

custom parts:
  HC-12 Module: HC-12 433Mhz Module
  HC-12 Antenna: Antenna for HC-12 433Mhz Module
